# Fritzing sketch Workshop_Sketch (saved by Fritzing 0.9.3b)
breadboards: 1

parts:
  Εξάρτημα1 = Arduino Uno (Rev3) - ICSP
  T1 = LM35 Temperature Sensor [package="TO92 [THT]"]
  LED1 = smd LED [color="Red (633nm)" package="0603 [SMD]"]

nets:
  N1: Εξάρτημα1.A0, T1.Vout
  N2: Εξάρτημα1.D13/SCK, LED1.anode
  GND: Εξάρτημα1.GND, T1.GND, LED1.cathode
  N3: Εξάρτημα1.5V, T1.+Vs
